// Logisim project 1-6.circ as structural Verilog: 1 circuit, main circuit main
module main (
  input  I,
  input  C,
  input  I_2,
  input  C1,
  input  [1:0] C2_C3,
  input  I_3,
  input  [1:0] C2_C3_2,
  input  CF,
  input  C1_2,
  output S1,
  output S2,
  output S1_2,
  output S2_2,
  output S3,
  output S4,
  output S5,
  output S6,
  output S7,
  output S8,
  output S1_3,
  output S2_3,
  output S3_2,
  output S4_2,
  output S5_2,
  output S6_2
);

  wire demultiplexer_1_out0, demultiplexer_1_out1, demultiplexer_3_out0, demultiplexer_3_out1;

  Demultiplexer #(.enable("false")) demultiplexer_1 (
    .out0(demultiplexer_1_out0), .out1(demultiplexer_1_out1), .in(I_3), .sel(CF));
  Demultiplexer #(.enable("false")) demultiplexer_2 (.out0(S1), .out1(S2), .in(I), .sel(C));
  Demultiplexer #(.enable("false")) demultiplexer_3 (
    .out0(demultiplexer_3_out0), .out1(demultiplexer_3_out1), .in(I_2), .sel(C1));
  Demultiplexer #(.select(2), .enable("false")) demultiplexer_4 (
    .out0(S1_2), .out1(S2_2), .out2(S3), .out3(S4), .in(demultiplexer_3_out0), .sel(C2_C3));
  Demultiplexer #(.select(2), .enable("false")) demultiplexer_5 (
    .out0(S5), .out1(S6), .out2(S7), .out3(S8), .in(demultiplexer_3_out1), .sel(C2_C3));
  Demultiplexer #(.select(2), .enable("false")) demultiplexer_6 (
    .out0(S1_3), .out1(S2_3), .out2(S3_2), .out3(S4_2), .in(demultiplexer_1_out0), .sel(C2_C3_2));
  Demultiplexer #(.enable("false")) demultiplexer_7 (.out0(S5_2), .out1(S6_2), .in(demultiplexer_1_out1), .sel(C1_2));

  // Notes on the sheet:
  //   DEMUX 1-2
  //   DEMUX 1-8
  //   DEMUX 1-6
endmodule
