// Logisim project 6-1.circ as structural Verilog: 1 circuit, main circuit main
module main (
  input  I1,
  input  I1_2,
  input  I2,
  input  in_4,
  input  I2_2,
  input  I3,
  input  in_7,
  input  I4,
  input  in_9,
  input  C,
  input  in_11,
  input  in_12,
  input  in_13,
  input  [2:0] in_14,
  input  I5,
  input  I6,
  input  I7,
  input  C1,
  input  I8,
  input  [1:0] C2_C3,
  input  I1_3,
  input  I2_3,
  input  I3_2,
  input  I4_2,
  input  [1:0] C2_C3_2,
  input  CF,
  input  I5_2,
  input  I6_2,
  input  C1_2,
  output S,
  output out_31,
  output out_32,
  output out_33
);

  wire multiplexer_2_out, multiplexer_3_out, multiplexer_4_out, multiplexer_5_out;

  Multiplexer #(.enable("false")) multiplexer_1 (.in0(I1_2), .in1(I2_2), .out(S), .sel(C));
  Multiplexer #(.select(2), .enable("false")) multiplexer_2 (
    .in0(I1), .in1(I2), .in2(I3), .in3(I4), .out(multiplexer_2_out), .sel(C2_C3));
  Multiplexer #(.select(2), .enable("false")) multiplexer_3 (
    .in0(I5), .in1(I6), .in2(I7), .in3(I8), .out(multiplexer_3_out), .sel(C2_C3));
  Multiplexer #(.select(2), .enable("false")) multiplexer_4 (
    .in0(I1_3), .in1(I2_3), .in2(I3_2), .in3(I4_2), .out(multiplexer_4_out), .sel(C2_C3_2));
  Multiplexer #(.enable("false")) multiplexer_5 (.in0(I5_2), .in1(I6_2), .out(multiplexer_5_out), .sel(C1_2));
  Multiplexer #(.enable("false")) multiplexer_6 (
    .in0(multiplexer_2_out), .in1(multiplexer_3_out), .out(out_32), .sel(C1));
  Multiplexer #(.enable("false")) multiplexer_7 (
    .in0(multiplexer_4_out), .in1(multiplexer_5_out), .out(out_33), .sel(CF));
  Multiplexer #(.select(3), .enable("false")) multiplexer_8 (
    .in0(in_4), .in1(in_7), .in2(in_9), .in3(in_11), .in4(in_12), .in5(in_13), .out(out_31), .sel(in_14));  // open: in6, in7

  // Notes on the sheet:
  //   MUX2-1
  //   MUX 8-1
  //   MUX 6-1
endmodule
