// Logisim project DEMUX 1-8.circ as structural Verilog: 1 circuit, main circuit main
module main (
  input  C2,
  input  C3,
  input  C2_2,
  input  C3_2,
  input  C1,
  input  CF,
  input  I,
  input  I_2,
  input  C1_2,
  output S1,
  output S1_2,
  output S2,
  output S2_2,
  output S3,
  output S3_2,
  output S4,
  output S4_2,
  output S5,
  output out_19,
  output S6,
  output out_21,
  output S7,
  output S8
);

  wire and_1_out, and_2_out, and_11_out, and_12_out;

  and and_1 (and_1_out, ~C1, I);  // AND_Gate
  and and_2 (and_2_out, C1, I);
  and and_3 (S1, ~C2, and_1_out, ~C3);  // AND_Gate
  and and_4 (S2, ~C2, and_1_out, C3);  // AND_Gate
  and and_5 (S3, C2, and_1_out, ~C3);  // AND_Gate
  and and_6 (S4, C2, and_1_out, C3);
  and and_7 (S5, ~C2, and_2_out, ~C3);  // AND_Gate
  and and_8 (S6, ~C2, and_2_out, C3);  // AND_Gate
  and and_9 (S7, C2, and_2_out, ~C3);  // AND_Gate
  and and_10 (S8, C2, and_2_out, C3);
  and and_11 (and_11_out, ~CF, I_2);  // AND_Gate
  and and_12 (and_12_out, CF, I_2);
  and and_13 (S1_2, ~C2_2, and_11_out, ~C3_2);  // AND_Gate
  and and_14 (S2_2, ~C2_2, and_11_out, C3_2);  // AND_Gate
  and and_15 (S3_2, C2_2, and_11_out, ~C3_2);  // AND_Gate
  and and_16 (S4_2, C2_2, and_11_out, C3_2);
  and and_17 (out_19, ~C1_2, and_12_out);  // AND_Gate
  and and_18 (out_21, C1_2, and_12_out);

  // Notes on the sheet:
  //   DEMUX 1-8
  //   DEMUX 1-6
endmodule
