// Logisim project MUX8-1.circ as structural Verilog: 1 circuit, main circuit main
module main (
  input  C2,
  input  C3,
  input  C1,
  input  I1,
  input  I2,
  input  I3,
  input  I4,
  input  I5,
  input  I6,
  input  I7,
  input  I8,
  output S
);

  wire and_1_out, and_2_out, and_3_out, and_4_out, and_5_out, and_6_out, and_7_out, and_8_out, and_9_out,
       and_10_out, or_1_out, or_2_out;

  and and_1 (and_1_out, ~C2, I1, ~C3);  // AND_Gate
  and and_2 (and_2_out, ~C2, I2, C3);  // AND_Gate
  and and_3 (and_3_out, C2, I3, ~C3);  // AND_Gate
  and and_4 (and_4_out, C2, I4, C3);
  and and_5 (and_5_out, ~C2, I5, ~C3);  // AND_Gate
  and and_6 (and_6_out, ~C2, I6, C3);  // AND_Gate
  and and_7 (and_7_out, C2, I7, ~C3);  // AND_Gate
  and and_8 (and_8_out, C2, I8, C3);
  or or_1 (or_1_out, and_1_out, and_2_out, and_3_out, and_4_out);
  or or_2 (or_2_out, and_5_out, and_6_out, and_7_out, and_8_out);
  and and_9 (and_9_out, ~C1, or_1_out);  // AND_Gate
  and and_10 (and_10_out, C1, or_2_out);
  or or_3 (S, and_9_out, and_10_out);
endmodule
