// Logisim project PRATICA_SD_01.circ as structural Verilog: 1 circuit, main circuit main
module main (
  input  A,
  input  B,
  input  C,
  output out_4
);

  wire and_1_out, and_2_out, and_3_out, and_4_out, and_5_out, and_6_out, and_7_out, and_8_out, and_9_out,
       and_10_out, not_1_out, not_2_out, not_3_out, not_4_out, not_5_out, not_6_out, not_7_out, not_8_out,
       not_9_out;

  and and_1 (and_1_out, A, A);
  not not_1 (not_1_out, and_1_out);
  not not_2 (not_2_out, and_2_out);
  and and_2 (and_2_out, B, B);
  and and_3 (and_3_out, C, C);
  not not_3 (not_3_out, and_3_out);
  and and_4 (and_4_out, not_1_out, not_2_out);
  not not_4 (not_4_out, and_4_out);
  and and_5 (and_5_out, not_1_out, not_3_out);
  not not_5 (not_5_out, and_5_out);
  and and_6 (and_6_out, not_4_out, not_4_out);
  and and_7 (and_7_out, not_5_out, not_5_out);
  not not_6 (not_6_out, and_6_out);
  not not_7 (not_7_out, and_7_out);
  and and_8 (and_8_out, not_6_out, not_6_out);
  and and_9 (and_9_out, not_7_out, not_7_out);
  not not_8 (not_8_out, and_8_out);
  not not_9 (not_9_out, and_9_out);
  and and_10 (and_10_out, not_8_out, not_9_out);
  not not_10 (out_4, and_10_out);
endmodule
