// Logisim project REVISAO.circ as structural Verilog: 1 circuit, main circuit main
module main (
  input  [3:0] A,
  input  [3:0] B,
  output [3:0] out_3
);

  wire [3:0] nand_1_out, nand_2_out, nand_3_out, nand_4_out, nand_5_out, nand_6_out, nand_7_out, nand_8_out;

  assign nand_1_out = ~(B & B);  // NAND_Gate nand_1, 4 bits wide
  assign nand_2_out = ~(A & nand_1_out);  // NAND_Gate nand_2, 4 bits wide
  assign nand_3_out = ~(A & A);  // NAND_Gate nand_3, 4 bits wide
  assign nand_4_out = ~(B & nand_3_out);  // NAND_Gate nand_4, 4 bits wide
  assign nand_5_out = ~(nand_2_out & nand_2_out);  // NAND_Gate nand_5, 4 bits wide
  assign nand_6_out = ~(nand_4_out & nand_4_out);  // NAND_Gate nand_6, 4 bits wide
  assign nand_7_out = ~(nand_6_out & nand_6_out);  // NAND_Gate nand_7, 4 bits wide
  assign nand_8_out = ~(nand_5_out & nand_5_out);  // NAND_Gate nand_8, 4 bits wide
  assign out_3 = ~(nand_8_out & nand_7_out);  // NAND_Gate nand_9, 4 bits wide
endmodule
