// Logisim project REVISAO_2.circ as structural Verilog: 1 circuit, main circuit main
module main (
  input  [3:0] A,
  input  [3:0] B,
  output [3:0] out_3
);

  wire [3:0] nor_1_out, nor_2_out, nor_3_out, nor_4_out, nor_5_out, nor_6_out, nor_7_out, nor_8_out,
       nor_9_out;

  assign nor_1_out = ~(B | B);  // NOR_Gate nor_1, 4 bits wide
  assign nor_2_out = ~(A | A);  // NOR_Gate nor_2, 4 bits wide
  assign nor_3_out = ~(A | A);  // NOR_Gate nor_3, 4 bits wide
  assign nor_4_out = ~(nor_1_out | nor_1_out);  // NOR_Gate nor_4, 4 bits wide
  assign nor_5_out = ~(nor_2_out | nor_2_out);  // NOR_Gate nor_5, 4 bits wide
  assign nor_6_out = ~(B | B);  // NOR_Gate nor_6, 4 bits wide
  assign nor_7_out = ~(nor_3_out | nor_4_out);  // NOR_Gate nor_7, 4 bits wide
  assign nor_8_out = ~(nor_5_out | nor_6_out);  // NOR_Gate nor_8, 4 bits wide
  assign nor_9_out = ~(nor_7_out | nor_8_out);  // NOR_Gate nor_9, 4 bits wide
  assign out_3 = ~(nor_9_out | nor_9_out);  // NOR_Gate nor_10, 4 bits wide
endmodule
