// Logisim project TESTEMUX.circ as structural Verilog: 1 circuit, main circuit main
module main (
  input  I1,
  input  I2,
  input  I3,
  input  I4,
  input  C2,
  input  C3,
  input  in_7,
  input  I5,
  input  I6,
  input  I7,
  input  I8,
  output out_12
);

  wire and_1_out, and_2_out, and_3_out, and_4_out, and_5_out, and_6_out, and_7_out, and_8_out, and_9_out,
       and_10_out, and_11_out, and_12_out, and_13_out, and_14_out, and_15_out, and_16_out, and_17_out,
       and_18_out, or_1_out, or_2_out;

  and and_1 (and_1_out, ~C2, ~C3);  // AND_Gate
  and and_2 (and_2_out, ~C2, C3);  // AND_Gate
  and and_3 (and_3_out, C2, ~C3);  // AND_Gate
  and and_4 (and_4_out, C2, C3);
  and and_5 (and_5_out, ~C2, ~C3);  // AND_Gate
  and and_6 (and_6_out, ~C2, C3);  // AND_Gate
  and and_7 (and_7_out, C2, ~C3);  // AND_Gate
  and and_8 (and_8_out, C2, C3);
  and and_9 (and_9_out, I1, and_1_out);
  and and_10 (and_10_out, I2, and_2_out);
  and and_11 (and_11_out, I3, and_3_out);
  and and_12 (and_12_out, I4, and_4_out);
  and and_13 (and_13_out, I5, and_5_out);
  and and_14 (and_14_out, I6, and_6_out);
  and and_15 (and_15_out, I7, and_7_out);
  and and_16 (and_16_out, I8, and_8_out);
  or or_1 (or_1_out, and_9_out, and_10_out, and_11_out, and_12_out);
  or or_2 (or_2_out, and_13_out, and_14_out, and_15_out, and_16_out);
  and and_17 (and_17_out, ~in_7, or_1_out);  // AND_Gate
  and and_18 (and_18_out, in_7, or_2_out);
  or or_3 (out_12, and_17_out, and_18_out);
endmodule
