// Logisim project TESTES.circ as structural Verilog: 1 circuit, main circuit main
module main (
  input  CLOCK,
  input  CLEAR,
  input  CLK,
  output Q0,
  output Q1,
  output F_OUT,
  output Q0_2,
  output Q1_2,
  output Q2,
  output Q3,
  output Q0_3,
  output Q1_3,
  output Q2_2,
  output Q3_2
);

  wire and_1_out, and_2_out, clock_1_out, not_1_out, not_2_out, not_3_out, not_4_out, or_1_out;

  Clock clock_1 (.out(clock_1_out));
  T_Flip_Flop #(.trigger("falling")) t_ff_1 (
    .clk(CLOCK), .T(1'b1), .Q(Q0_2), .reset(or_1_out));  // open: Qn, preset, en
  or or_1 (or_1_out, CLEAR, and_1_out);
  T_Flip_Flop #(.trigger("falling")) t_ff_2 (.clk(CLK), .T(1'b1), .Q(Q0_3), .reset(and_2_out));  // open: Qn, preset, en
  T_Flip_Flop #(.trigger("falling")) t_ff_3 (.clk(clock_1_out), .T(1'b1), .Q(Q0));  // open: Qn, preset, reset, en
  T_Flip_Flop #(.trigger("falling")) t_ff_4 (.clk(Q0), .T(1'b1), .Q(Q1));  // open: Qn, preset, reset, en
  T_Flip_Flop #(.trigger("falling")) t_ff_5 (.clk(Q0_2), .T(1'b1), .Q(Q1_2), .reset(or_1_out));  // open: Qn, preset, en
  not not_1 (not_1_out, Q2);
  not not_2 (not_2_out, Q0_2);
  and and_1 (and_1_out, not_2_out, Q1_2, not_1_out, Q3);
  T_Flip_Flop #(.trigger("falling")) t_ff_6 (
    .clk(Q0_3), .T(1'b1), .Q(Q1_3), .reset(and_2_out));  // open: Qn, preset, en
  not not_3 (not_3_out, Q0_3);
  not not_4 (not_4_out, Q2_2);
  and and_2 (and_2_out, not_3_out, Q1_3, not_4_out, Q3_2);
  T_Flip_Flop #(.trigger("falling")) t_ff_7 (.clk(Q1), .T(1'b1), .Q(F_OUT));  // open: Qn, preset, reset, en
  T_Flip_Flop #(.trigger("falling")) t_ff_8 (.clk(Q1_2), .T(1'b1), .Q(Q2), .reset(or_1_out));  // open: Qn, preset, en
  T_Flip_Flop #(.trigger("falling")) t_ff_9 (
    .clk(Q2_2), .T(1'b1), .Q(Q3_2), .reset(and_2_out));  // open: Qn, preset, en
  T_Flip_Flop #(.trigger("falling")) t_ff_10 (
    .clk(Q1_3), .T(1'b1), .Q(Q2_2), .reset(and_2_out));  // open: Qn, preset, en
  T_Flip_Flop #(.trigger("falling")) t_ff_11 (.clk(Q2), .T(1'b1), .Q(Q3), .reset(or_1_out));  // open: Qn, preset, en
endmodule
