// Logisim project contador_binario.circ as structural Verilog: 1 circuit, main circuit main
module main (
  output Q0,
  output Q1,
  output Q2,
  output Q0_2,
  output Q1_2,
  output Q2_2
);

  wire clock_1_out, clock_2_out, t_ff_2_qn, t_ff_5_qn;

  Clock clock_1 (.out(clock_1_out));
  Clock clock_2 (.out(clock_2_out));
  T_Flip_Flop #(.trigger("falling")) t_ff_1 (.clk(clock_2_out), .T(1'b1), .Q(Q0));  // open: Qn, preset, reset, en
  T_Flip_Flop #(.trigger("falling")) t_ff_2 (
    .clk(clock_1_out), .T(1'b1), .Q(Q0_2), .Qn(t_ff_2_qn));  // open: preset, reset, en
  T_Flip_Flop #(.trigger("falling")) t_ff_3 (.clk(Q1), .T(1'b1), .Q(Q2));  // open: Qn, preset, reset, en
  T_Flip_Flop #(.trigger("falling")) t_ff_4 (.clk(Q0), .T(1'b1), .Q(Q1));  // open: Qn, preset, reset, en
  T_Flip_Flop #(.trigger("falling")) t_ff_5 (
    .clk(t_ff_2_qn), .T(1'b1), .Q(Q1_2), .Qn(t_ff_5_qn));  // open: preset, reset, en
  T_Flip_Flop #(.trigger("falling")) t_ff_6 (.clk(t_ff_5_qn), .T(1'b1), .Q(Q2_2));  // open: Qn, preset, reset, en

  // Notes on the sheet:
  //   CONTADOR CRESCENTE
  //   CONTADOR DECRESCENTE
endmodule
