// Logisim project desloca_direita.circ as structural Verilog: 1 circuit, main circuit main
module main (
  input  CLK,
  input  FILL,
  input  CLEAR,
  input  ENABLE,
  input  D0,
  input  D1,
  input  D2,
  input  D3,
  input  D4,
  input  D5,
  input  D6,
  input  D7,
  output S0,
  output S1,
  output S2,
  output S3,
  output S4,
  output S5,
  output S6,
  output S7
);

  wire and_1_out, and_2_out, and_3_out, and_4_out, and_5_out, and_6_out, and_7_out, and_8_out;

  and and_1 (and_1_out, ENABLE, D0);
  D_Flip_Flop d_ff_1 (.clk(CLK), .D(FILL), .Q(S0), .preset(and_1_out), .reset(CLEAR));  // open: Qn, en
  D_Flip_Flop d_ff_2 (.clk(CLK), .D(S0), .Q(S1), .preset(and_2_out), .reset(CLEAR));  // open: Qn, en
  and and_2 (and_2_out, ENABLE, D1);
  D_Flip_Flop d_ff_3 (.clk(CLK), .D(S1), .Q(S2), .preset(and_3_out), .reset(CLEAR));  // open: Qn, en
  and and_3 (and_3_out, ENABLE, D2);
  and and_4 (and_4_out, ENABLE, D3);
  D_Flip_Flop d_ff_4 (.clk(CLK), .D(S2), .Q(S3), .preset(and_4_out), .reset(CLEAR));  // open: Qn, en
  and and_5 (and_5_out, ENABLE, D4);
  D_Flip_Flop d_ff_5 (.clk(CLK), .D(S4), .Q(S5), .preset(and_6_out), .reset(CLEAR));  // open: Qn, en
  D_Flip_Flop d_ff_6 (.clk(CLK), .D(S3), .Q(S4), .preset(and_5_out), .reset(CLEAR));  // open: Qn, en
  and and_6 (and_6_out, ENABLE, D5);
  D_Flip_Flop d_ff_7 (.clk(CLK), .D(S5), .Q(S6), .preset(and_8_out), .reset(CLEAR));  // open: Qn, en
  and and_7 (and_7_out, ENABLE, D7);
  and and_8 (and_8_out, ENABLE, D6);
  D_Flip_Flop d_ff_8 (.clk(CLK), .D(S6), .Q(S7), .preset(and_7_out), .reset(CLEAR));  // open: Qn, en
endmodule
