// Logisim project muxdemux.circ as structural Verilog: 1 circuit, main circuit main
module main (
  input  A,
  input  B,
  input  C,
  input  A_2,
  input  C_2,
  output S1,
  output S,
  output S2
);

  wire and_1_out, and_2_out, not_1_out, not_2_out;

  not not_1 (not_1_out, C);
  and and_1 (and_1_out, not_1_out, A);
  and and_2 (and_2_out, B, C);
  or or_1 (S, and_1_out, and_2_out);
  not not_2 (not_2_out, C_2);
  and and_3 (S1, A_2, not_2_out);
  and and_4 (S2, A_2, C_2);
endmodule
