// Logisim project parelo_serial.circ as structural Verilog: 1 circuit, main circuit main
module main (
  input  CLOCK,
  input  CLEAR,
  input  ENABLE,
  input  D7,
  input  D6,
  input  D5,
  input  D4,
  input  D3,
  input  D2,
  input  D1,
  input  D0,
  input  CLOCK_2,
  input  I,
  output out_14,
  output S7,
  output S6,
  output S5,
  output S4,
  output S3,
  output S2,
  output S1,
  output S0
);

  wire and_1_out, and_2_out, and_3_out, and_4_out, and_5_out, and_6_out, and_7_out, and_8_out, d_ff_1_q,
       d_ff_2_q, d_ff_4_q, d_ff_6_q, d_ff_8_q, d_ff_9_q, d_ff_12_q;

  and and_1 (and_1_out, ENABLE, D7);
  D_Flip_Flop d_ff_1 (.clk(CLOCK), .D(d_ff_2_q), .Q(d_ff_1_q), .preset(and_2_out), .reset(CLEAR));  // open: Qn, en
  D_Flip_Flop d_ff_2 (.clk(CLOCK), .D(1'b0), .Q(d_ff_2_q), .preset(and_1_out), .reset(CLEAR));  // open: Qn, en
  and and_2 (and_2_out, ENABLE, D6);
  D_Flip_Flop d_ff_3 (.clk(CLOCK_2), .D(I), .Q(S7));  // open: Qn, preset, en, reset
  D_Flip_Flop d_ff_4 (.clk(CLOCK), .D(d_ff_1_q), .Q(d_ff_4_q), .preset(and_4_out), .reset(CLEAR));  // open: Qn, en
  and and_3 (and_3_out, ENABLE, D4);
  and and_4 (and_4_out, ENABLE, D5);
  D_Flip_Flop d_ff_5 (.clk(CLOCK_2), .D(S7), .Q(S6));  // open: Qn, preset, en, reset
  D_Flip_Flop d_ff_6 (.clk(CLOCK), .D(d_ff_4_q), .Q(d_ff_6_q), .preset(and_3_out), .reset(CLEAR));  // open: Qn, en
  and and_5 (and_5_out, ENABLE, D3);
  D_Flip_Flop d_ff_7 (.clk(CLOCK_2), .D(S6), .Q(S5));  // open: Qn, preset, en, reset
  D_Flip_Flop d_ff_8 (.clk(CLOCK), .D(d_ff_9_q), .Q(d_ff_8_q), .preset(and_6_out), .reset(CLEAR));  // open: Qn, en
  D_Flip_Flop d_ff_9 (.clk(CLOCK), .D(d_ff_6_q), .Q(d_ff_9_q), .preset(and_5_out), .reset(CLEAR));  // open: Qn, en
  and and_6 (and_6_out, ENABLE, D2);
  D_Flip_Flop d_ff_10 (.clk(CLOCK_2), .D(S4), .Q(S3));  // open: Qn, preset, en, reset
  D_Flip_Flop d_ff_11 (.clk(CLOCK_2), .D(S5), .Q(S4));  // open: Qn, preset, en, reset
  D_Flip_Flop d_ff_12 (.clk(CLOCK), .D(d_ff_8_q), .Q(d_ff_12_q), .preset(and_7_out), .reset(CLEAR));  // open: Qn, en
  and and_7 (and_7_out, ENABLE, D1);
  and and_8 (and_8_out, ENABLE, D0);
  D_Flip_Flop d_ff_13 (.clk(CLOCK_2), .D(S3), .Q(S2));  // open: Qn, preset, en, reset
  D_Flip_Flop d_ff_14 (.clk(CLOCK), .D(d_ff_12_q), .Q(out_14), .preset(and_8_out), .reset(CLEAR));  // open: Qn, en
  D_Flip_Flop d_ff_15 (.clk(CLOCK_2), .D(S2), .Q(S1));  // open: Qn, preset, en, reset
  D_Flip_Flop d_ff_16 (.clk(CLOCK_2), .D(S1), .Q(S0));  // open: Qn, preset, en, reset
endmodule
